# Fritzing sketch Esquema Estufa Inteligente (saved by Fritzing 0.9.3b)
breadboards: 1

parts:
  DHT11 = DHT11 Humitidy and Temperature Sensor
  Temperarura_e_Umidade_A_prova_d'agua = DS18B20 1-Wire Temperature Sensor [part_number=DS18B20]
  FC_-_28_Umidade_do_Solo = FC-28 Soil Hygrometer Module
  Componente1 = Arduino Leonardo (Rev3b)
  R1 = Resistor [tolerance=±5% resistance=4.7k package="0402 [SMD]"]

nets:
  VDD: DHT11.VDD, Temperarura_e_Umidade_A_prova_d'agua.VDD, FC_-_28_Umidade_do_Solo.VCC, Componente1.5V, R1.Pin_1
  N1: DHT11.DATA, Componente1.A0
  GND: DHT11.GND, Temperarura_e_Umidade_A_prova_d'agua.GND, FC_-_28_Umidade_do_Solo.GND, Componente1.GND
  N2: Temperarura_e_Umidade_A_prova_d'agua.DQ, Componente1.D2/SDA, R1.Pin_0
  N3: FC_-_28_Umidade_do_Solo.AO, Componente1.D7

custom parts:
  DHT11 Humitidy and Temperature Sensor: DHT11 Humidity and Temperature Sensor
  FC-28 Soil Hygrometer Module: The FC-28 is a soil hygrometer module that uses the Texas Instruments LM393 comparator chip to provide an analog measurement of soil humidity. The digital output is high when soil moisture is over a certain threshold, as determined by adjusting the potentiometer.
